# Fritzing sketch dht11 (saved by Fritzing 0.9.6b)
breadboards: 2

parts:
  MH-ET_LIVE_ESP32_DEVKIT1 = MH-ET LIVE ESP32 DEVKIT 38 pins
  M1 = Humidity and Temperature Sensor DHT11
  R4 = Resistor [tolerance=±5% power=0.25 resistance=10k package=THT]

nets:
  N1: MH-ET_LIVE_ESP32_DEVKIT1.GND#64, M1.GND
  N2: MH-ET_LIVE_ESP32_DEVKIT1.IO4, M1.Data, R4.Pin_1
  N3: M1.Vcc, R4.Pin_0

custom parts:
  MH-ET LIVE ESP32 DEVKIT 38 pins: http://mh.nodebb.com/topic/2/mh-et-live-esp32-devkit
  Humidity and Temperature Sensor DHT11: Digital relative humidity & temperature sensor DHT11
