# Fritzing sketch final (saved by Fritzing 0.9.6b)
breadboards: 2

parts:
  MH-ET_LIVE_ESP32_DEVKIT1 = MH-ET LIVE ESP32 DEVKIT 38 pins
  R1 = Resistor [tolerance=±5% power=0.25 resistance=100 package=THT]
  LED1 = LED - 5mm [color="Red (633nm)" current=0.030 package="5 mm [THT]"]
  S1 = Pushbutton [package="[THT]"]
  OLED1 = OLED 128x64 I2C Monochrome Display GND-VDD
  R2 = Resistor [tolerance=±5% power=0.25 resistance=10k package=THT]
  R3 = Resistor [tolerance=±5% power=0.25 resistance=10k package=THT]
  M1 = Humidity and Temperature Sensor DHT11
  R4 = Resistor [tolerance=±5% power=0.25 resistance=10k package=THT]

nets:
  3V3: MH-ET_LIVE_ESP32_DEVKIT1.3V3, OLED1.VDD, R2.Pin_1, R3.Pin_1, M1.Vcc, R4.Pin_0
  N1: MH-ET_LIVE_ESP32_DEVKIT1.SVP, LED1.anode
  N2: MH-ET_LIVE_ESP32_DEVKIT1.GND#58, R1.Pin_0, OLED1.GND
  N3: MH-ET_LIVE_ESP32_DEVKIT1.GND#64, S1.Pin_3, S1.Pin_4, M1.GND
  N4: MH-ET_LIVE_ESP32_DEVKIT1.IO22, OLED1.SDA, R2.Pin_0
  N5: MH-ET_LIVE_ESP32_DEVKIT1.IO21, OLED1.SCK, R3.Pin_0
  N6: MH-ET_LIVE_ESP32_DEVKIT1.IO5, S1.Pin_1, S1.Pin_2
  N7: MH-ET_LIVE_ESP32_DEVKIT1.IO4, M1.Data, R4.Pin_1
  N8: R1.Pin_1, LED1.cathode

custom parts:
  MH-ET LIVE ESP32 DEVKIT 38 pins: http://mh.nodebb.com/topic/2/mh-et-live-esp32-devkit
  OLED 128x64 I2C Monochrome Display GND-VDD: OLED 128x64 I2C Monochrome Display. Note: there are two variants of this part, this one is the GND VDD SCK SDA variant. The other is VDD GND SCK SDA. Make sure you select the part that matches your module as using the incorrect part will probably destroy your module! In addition the mounting holes are marked on silkscreen but not by default drilled. If you want drilled mounting holes, copy a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
  Humidity and Temperature Sensor DHT11: Digital relative humidity & temperature sensor DHT11
