# Fritzing sketch switch (saved by Fritzing 0.9.6b)
breadboards: 2

parts:
  MH-ET_LIVE_ESP32_DEVKIT1 = MH-ET LIVE ESP32 DEVKIT 38 pins
  R1 = Resistor [tolerance=±5% power=0.25 resistance=100 package=THT]
  LED1 = LED - 5mm [color="Red (633nm)" current=0.030 package="5 mm [THT]"]
  S1 = Pushbutton [package="[THT]"]
  LED2 = LED - 5mm [color="Red (633nm)" current=0.030 package="5 mm [THT]"]
  R2 = Resistor [tolerance=±5% power=0.25 resistance=100 package=THT]

nets:
  N1: MH-ET_LIVE_ESP32_DEVKIT1.IO12, LED2.anode
  N2: MH-ET_LIVE_ESP32_DEVKIT1.GND#58, R1.Pin_0, R2.Pin_1
  N3: MH-ET_LIVE_ESP32_DEVKIT1.IO13, LED1.anode
  N4: MH-ET_LIVE_ESP32_DEVKIT1.GND#64, S1.Pin_3, S1.Pin_4
  N5: MH-ET_LIVE_ESP32_DEVKIT1.IO2, S1.Pin_1, S1.Pin_2
  N6: R1.Pin_1, LED1.cathode
  N7: LED2.cathode, R2.Pin_0

custom parts:
  MH-ET LIVE ESP32 DEVKIT 38 pins: http://mh.nodebb.com/topic/2/mh-et-live-esp32-devkit
